# Fritzing sketch ElectricalScheme (saved by Fritzing 0.9.6b)
breadboards: 1

parts:
  A1 = DM860A Stepper Motor Driver
  Pololu_A1 = Pololu A4988 [package=SO16]
  Raspberry_Pi_1 = Raspberry Pi 4 [part_number=RPI-4-b]
  M2 = Stepper Motor - Bipolar
  alim = Stepper Motor - Bipolar
  S1 = D2F-FL Omron Snap Action Limit Switch with Level
  VCC1 = Battery block 9V
  JACK1 = 2.1mm Barrel Jack with Terminal Block

nets:
  N1: A1.B-, alim.D
  N2: A1.B+, alim.B
  N3: A1.A-, alim.A
  N4: A1.A+, alim.C
  N5: A1.VDC, JACK1.POS
  N6: A1.GND, JACK1.NEG
  GND: A1.ENBL-(ENB), Pololu_A1.GND, Raspberry_Pi_1.GND, S1.Pin_3, VCC1.-
  N7: A1.ENBL+(+5V), Raspberry_Pi_1.GPIO22
  N8: A1.DIR+(+5V), Raspberry_Pi_1.GPIO17
  N9: A1.PUL+(+5V), Raspberry_Pi_1.GPIO27
  N10: Pololu_A1.MS3, Raspberry_Pi_1.GPIO11
  N11: Pololu_A1.RESET, Pololu_A1.SLEEP
  N12: Pololu_A1.STEP, Raspberry_Pi_1.GPIO9
  N13: Pololu_A1.DIR, Raspberry_Pi_1.GPIO10
  VDD: Pololu_A1.VDD, Raspberry_Pi_1.3v3
  N14: Pololu_A1.1B, M2.A
  N15: Pololu_A1.1A, M2.C
  N16: Pololu_A1.2A, M2.B
  N17: Pololu_A1.2B, M2.D
  N18: Pololu_A1.VMOT, VCC1.+
  N19: Raspberry_Pi_1.GPIO8, S1.Pin_1

custom parts:
  DM860A Stepper Motor Driver: DM860A is a type of two-phase hybrid stepping motor driver, The drive voltage of which is from 24VDC to 80VDC. It is designed for use with 2-phase hybrid stepper motor of all kinds with 57mm to 110mm outside diameter and less than 8.0A phase current. Mar 2023: Correct pcb layerId as the part won't save correctly in a .fzz file as is.
  Raspberry Pi 4: The RPi4, a faster version of the awesome Raspberry Pi 2 B ARM Board with 40 pin gpio. Ready for special Raspberry Pi B+ and RPi2 Hat (Hardware attached (on) top)
  D2F-FL Omron Snap Action Limit Switch with Level: Snap action switch with stainless steel lever.
